# Fritzing sketch motor (saved by Fritzing 0.9.3b)
breadboards: 1

parts:
  IC2 = ULN2003A [package="SO16 [SMD]"]
  Part1 = Arduino Uno (Rev3) - ICSP
  BAT1 = Battery Holders [package=battery-aa]
  BAT2 = Battery Holders [package=battery-aa]
  BAT3 = Battery Holders [package=battery-aa]

nets:
  N1: IC2.In_1, Part1.D11_PWM/MOSI
  N2: IC2.In_2, Part1.D10_PWM/SS
  N3: IC2.In_3, Part1.D9_PWM
  N4: IC2.In_4, Part1.D8
  N5: IC2.0V, Part1.GND, BAT1.+
  N6: BAT1.-, BAT2.+
  N7: BAT2.-, BAT3.+

notes:
  步进电机
  触发装置
